// Logisim project bp.circ as structural Verilog: 2 circuits, main circuit main
module main (
  input  [7:0] PC,
  input  BRANCH_TAKEN,
  input  in_3,
  input  in_4,
  input  in_5,
  input  in_6
);

  wire clock_1_out, control_1_counter_e, control_1_counter_id, control_1_counter_l, control_1_pcse,
       control_1_ram_oe, control_1_ram_we, not_1_out;
  wire [2:0] counter_1_q;
  wire [7:0] BHT_dout, INC_DEC_q, PCS_q;

  Clock clock_1 (.out(clock_1_out));
  // Probe on BHT_dout[1]
  RAM BHT (
    .addr(PCS_q), .we(control_1_ram_we), .oe(control_1_ram_oe), .clk(clock_1_out), .din(INC_DEC_q),
    .dout(BHT_dout));
  Counter #(.max('h7), .width(3)) counter_1 (
    .count(in_5), .Q(counter_1_q), .clk(not_1_out), .clr(in_6));  // open: load, D, carry, up
  not not_1 (not_1_out, clock_1_out);
  Register PCS (.D(PC), .en(control_1_pcse), .Q(PCS_q), .clk(clock_1_out), .clr(in_4));
  control control_1 (
    .branch_ip(BRANCH_TAKEN), .bit_2(counter_1_q[2]), .bit_1(counter_1_q[1]), .bit_0(counter_1_q[0]),
    .pcse(control_1_pcse), .counter_id(control_1_counter_id), .ram_oe(control_1_ram_oe),
    .counter_l(control_1_counter_l), .ram_we(control_1_ram_we), .counter_e(control_1_counter_e));
  Counter INC_DEC (
    .load(control_1_counter_l), .D(BHT_dout), .count(control_1_counter_e), .Q(INC_DEC_q),
    .up(control_1_counter_id), .clk(clock_1_out), .clr(in_3));  // open: carry
  // Probe on BHT_dout
endmodule

module control (
  input  branch_ip,
  input  bit_2,
  input  bit_1,
  input  bit_0,
  output pcse,
  output counter_id,
  output ram_oe,
  output counter_l,
  output ram_we,
  output counter_e
);

  wire and_2_out, and_3_out, and_4_out, and_5_out, and_6_out, and_7_out, and_8_out, and_9_out, and_10_out,
       and_11_out, and_12_out, and_13_out, not_1_out, not_2_out, not_3_out, not_4_out;

  not not_1 (not_1_out, branch_ip);
  not not_2 (not_2_out, bit_2);
  not not_3 (not_3_out, bit_1);
  not not_4 (not_4_out, bit_0);
  and and_1 (pcse, not_1_out, not_2_out, not_3_out, bit_0);
  and and_2 (and_2_out, branch_ip, not_2_out, not_3_out, bit_0);
  and and_3 (and_3_out, branch_ip, not_2_out, bit_1, not_4_out);
  and and_4 (and_4_out, not_1_out, not_2_out, bit_1);
  and and_5 (and_5_out, branch_ip, not_2_out, not_3_out, bit_0);
  and and_6 (and_6_out, not_1_out, not_2_out, bit_1, bit_0);
  and and_7 (and_7_out, branch_ip, not_2_out, not_3_out, bit_0);
  and and_8 (and_8_out, not_1_out, bit_2, not_3_out, bit_0);
  and and_9 (and_9_out, branch_ip, not_2_out, bit_1, bit_0);
  and and_10 (and_10_out, not_1_out, not_2_out, bit_1, bit_0);
  and and_11 (and_11_out, not_1_out, bit_2, not_3_out, not_4_out);
  and and_12 (and_12_out, branch_ip, not_2_out, not_3_out, bit_0);
  and and_13 (and_13_out, branch_ip, not_2_out, bit_1, not_4_out);
  or or_1 (counter_id, and_2_out, and_3_out);
  or or_2 (ram_oe, and_4_out, and_5_out);
  or or_3 (counter_l, and_6_out, and_7_out);
  or or_4 (ram_we, and_8_out, and_9_out);
  or or_5 (counter_e, and_10_out, and_11_out, and_12_out, and_13_out);
endmodule
